// Logisim project jcbraun-project1.circ as structural Verilog: 8 circuits, main circuit main
module main (
  input  in_1,
  input  in_2,
  input  in_3,
  input  in_4
);

  wire bottombar_1_out_5, bottomleft_1_out_5, bottomright_1_out_5, middlebar_1_out_5, topbar_1_out_5,
       topleft_1_out_5, topright_1_out_5;

  bottomleft bottomleft_1 (.A(in_4), .B(in_1), .C(in_2), .D(in_3), .out_5(bottomleft_1_out_5));
  middlebar middlebar_1 (.C(in_2), .B(in_1), .A(in_4), .D(in_3), .out_5(middlebar_1_out_5));
  topleft topleft_1 (.A(in_4), .B(in_1), .C(in_2), .D(in_3), .out_5(topleft_1_out_5));
  topbar topbar_1 (.A(in_4), .B(in_1), .C(in_2), .D(in_3), .out_5(topbar_1_out_5));
  _7_Segment_Display u_7_segment_display_1 (
    .g(middlebar_1_out_5), .f(topleft_1_out_5), .a(topbar_1_out_5), .b(topright_1_out_5),
    .e(bottomleft_1_out_5), .d(bottombar_1_out_5), .c(bottomright_1_out_5));  // open: dp
  bottombar bottombar_1 (.C(in_2), .D(in_3), .A(in_4), .B(in_1), .out_5(bottombar_1_out_5));
  topright topright_1 (.A(in_4), .B(in_1), .C(in_2), .D(in_3), .out_5(topright_1_out_5));
  bottomright bottomright_1 (.A(in_4), .B(in_1), .C(in_2), .D(in_3), .out_5(bottomright_1_out_5));
endmodule

module middlebar (
  input  C,
  input  B,
  input  A,
  input  D,
  output out_5
);

  wire and_1_out, and_2_out, and_3_out, not_1_out, not_2_out, not_3_out;

  or or_1 (out_5, A, and_1_out, and_3_out, and_2_out);
  and and_1 (and_1_out, C, not_1_out);
  and and_2 (and_2_out, B, not_2_out);
  not not_1 (not_1_out, B);
  not not_2 (not_2_out, C);
  not not_3 (not_3_out, D);
  and and_3 (and_3_out, not_3_out, C);

  // Notes on the sheet:
  //   A
  //   B
  //   C
  //   D
endmodule

module topbar (
  input  A,
  input  B,
  input  C,
  input  D,
  output out_5
);

  wire and_1_out, and_2_out, not_1_out, not_2_out;

  and and_1 (and_1_out, D, B);
  or or_1 (out_5, A, and_1_out, C, and_2_out);
  not not_1 (not_1_out, B);
  not not_2 (not_2_out, D);
  and and_2 (and_2_out, not_2_out, not_1_out);
endmodule

module topleft (
  input  A,
  input  B,
  input  C,
  input  D,
  output out_5
);

  wire and_1_out, and_2_out, and_3_out, not_1_out, not_2_out, not_3_out, or_1_out;

  not not_1 (not_1_out, B);
  and and_1 (and_1_out, A, not_1_out);
  not not_2 (not_2_out, C);
  not not_3 (not_3_out, D);
  and and_2 (and_2_out, B, or_1_out);
  and and_3 (and_3_out, not_2_out, not_3_out);
  or or_1 (or_1_out, not_2_out, not_3_out);
  or or_2 (out_5, and_2_out, and_3_out, and_1_out);
endmodule

module topright (
  input  A,
  input  B,
  input  C,
  input  D,
  output out_5
);

  wire and_1_out, and_2_out, not_1_out, not_2_out, not_3_out;

  or or_1 (out_5, not_1_out, and_2_out, and_1_out);
  not not_1 (not_1_out, B);
  and and_1 (and_1_out, D, C);
  not not_2 (not_2_out, D);
  not not_3 (not_3_out, C);
  and and_2 (and_2_out, not_2_out, not_3_out);
endmodule

module bottomright (
  input  A,
  input  B,
  input  C,
  input  D,
  output out_5
);

  wire and_1_out, not_1_out, not_2_out, not_3_out;

  not not_1 (not_1_out, A);
  not not_2 (not_2_out, B);
  and and_1 (and_1_out, not_3_out, C, not_2_out, not_1_out);
  not not_3 (not_3_out, D);
  not not_4 (out_5, and_1_out);
endmodule

module bottombar (
  input  C,
  input  D,
  input  A,
  input  B,
  output out_5
);

  wire and_1_out, and_2_out, and_3_out, CD_prime_out, not_1_out, not_2_out, not_3_out;

  and and_1 (and_1_out, not_1_out, not_3_out);
  not not_1 (not_1_out, B);
  not not_2 (not_2_out, C);
  or or_1 (out_5, and_1_out, and_3_out, and_2_out, CD_prime_out);
  and CD_prime (CD_prime_out, C, not_3_out);
  not not_3 (not_3_out, D);
  and and_2 (and_2_out, C, not_1_out);
  and and_3 (and_3_out, not_2_out, B, D);
endmodule

module bottomleft (
  input  A,
  input  B,
  input  C,
  input  D,
  output out_5
);

  wire and_1_out, and_2_out, not_1_out, not_2_out;

  not not_1 (not_1_out, B);
  or or_1 (out_5, and_2_out, and_1_out);
  and and_1 (and_1_out, not_1_out, not_2_out);
  not not_2 (not_2_out, D);
  and and_2 (and_2_out, C, not_2_out);
endmodule
